// Logisim project Modul5_Enkoder dan Dekoder.circ as structural Verilog: 1 circuit, main circuit main
module main (
  input  B0,
  input  B1,
  input  B2,
  input  B3,
  input  _0,
  input  _1,
  input  _2,
  input  _3,
  input  _4,
  input  _5,
  input  _6,
  input  _7,
  input  _8,
  output _0_2,
  output _1_2,
  output _2_2,
  output _3_2,
  output _4_2,
  output _5_2,
  output _6_2,
  output _7_2,
  output _8_2,
  output B0_2,
  output B1_2,
  output B2_2,
  output B3_2
);

  // DIP_7442 dip_7442_1: pin names not known; wires that end beside it: _0_2, _1_2, _2_2, _3_2, _4_2, _5_2, _6_2, B0, B1, B2, B3, _7_2, _8_2, _6_2
  // DIP_74147 dip_74147_1: pin names not known; wires that end beside it: _3, _8, _3, _4, _5, _6, _7, B2_2, B1_2, B3_2, _2, _1, _0, _8, B0_2, B3_2

  // Notes on the sheet:
  //   IC 7442 (DEKODER)
  //   IC 74147 (ENKODER)
endmodule
